// Logisim project ICTester.circ as structural Verilog
module Matching_5Not_1Or_8And (
  input  g0,
  input  g1,
  input  g2,
  input  g3,
  input  test,
  output f
);

  wire and_1_out, and_2_out, and_3_out, and_4_out, and_5_out, and_6_out, and_7_out, and_8_out, not_1_out,
       not_2_out, not_3_out, not_4_out, not_5_out;

  not not_1 (not_1_out, g0);
  not not_2 (not_2_out, g1);
  and and_1 (and_1_out, not_1_out, not_2_out);
  not not_3 (not_3_out, g2);
  not not_4 (not_4_out, g3);
  not not_5 (not_5_out, test);
  and and_2 (and_2_out, g0, g1);
  and and_3 (and_3_out, and_1_out, not_3_out);
  and and_4 (and_4_out, and_3_out, and_5_out);
  and and_5 (and_5_out, not_4_out, not_5_out);
  and and_6 (and_6_out, and_2_out, g2);
  and and_7 (and_7_out, and_6_out, and_8_out);
  and and_8 (and_8_out, g3, test);
  or or_1 (f, and_4_out, and_7_out);
endmodule

module Matching_1Not_5Or_4And (
  input  test,
  input  g0,
  input  g1,
  input  g2,
  input  g3,
  output f
);

  wire and_1_out, and_2_out, and_3_out, and_4_out, nor_1_out, or_1_out, or_2_out, or_3_out;

  or or_1 (or_1_out, g0, g1);
  and and_1 (and_1_out, g0, g1);
  or or_2 (or_2_out, or_1_out, g2);
  or or_3 (or_3_out, g3, test);
  and and_2 (and_2_out, and_1_out, g2);
  and and_3 (and_3_out, g3, test);
  nor nor_1 (nor_1_out, or_2_out, or_3_out);
  and and_4 (and_4_out, and_2_out, and_3_out);
  or or_4 (f, nor_1_out, and_4_out);
endmodule

module Matching_4Xor_3And (
  input  test,
  input  g0,
  input  g1,
  input  g2,
  input  g3,
  output f
);

  wire and_1_out, and_2_out, xnor_1_out, xnor_2_out, xnor_3_out, xnor_4_out;

  xnor xnor_1 (xnor_1_out, test, g0);
  xnor xnor_2 (xnor_2_out, test, g1);
  xnor xnor_3 (xnor_3_out, test, g2);
  xnor xnor_4 (xnor_4_out, test, g3);
  and and_1 (and_1_out, xnor_1_out, xnor_2_out);
  and and_2 (and_2_out, xnor_3_out, xnor_4_out);
  and and_3 (f, and_1_out, and_2_out);
endmodule
